// Logisim project cpu.circ as structural Verilog: 3 circuits, main circuit main
module main (
  input  [3:0] in_1,
  input  in_2,
  input  addr_src,
  input  IR_write,
  input  PC_write,
  input  mem_write,
  input  DATA_write,
  input  in_8,
  input  in_9
);

  wire alu_1_c_out, alu_1_n, alu_1_v, alu_1_z, CLOCK_out, not_1_out;
  wire [7:0] ADDR_LO_q, DATA_q, IR_q, ram_1_data;
  wire [15:0] alu_1_result, multiplexer_1_out, PC_q;
  wire [15:8] ADDR_HI_q;

  Clock CLOCK (.out(CLOCK_out));
  Register #(.width(16)) PC (.D(alu_1_result), .en(PC_write), .Q(PC_q), .clk(CLOCK_out));  // open: clr
  Multiplexer #(.width(16)) multiplexer_1 (
    .in0(PC_q), .in1({ADDR_HI_q, ADDR_LO_q}), .out(multiplexer_1_out), .sel(addr_src));
  not not_1 (not_1_out, mem_write);
  RAM #(.addrWidth(16)) ram_1 (
    .addr(multiplexer_1_out), .data(ram_1_data), .sel(not_1_out), .clk(CLOCK_out), .ld(not_1_out));  // open: clr
  Register ADDR_HI (.D(ram_1_data), .en(in_9), .Q(ADDR_HI_q), .clk(CLOCK_out));  // open: clr
  Register ADDR_LO (.D(ram_1_data), .en(in_8), .Q(ADDR_LO_q), .clk(CLOCK_out));  // open: clr
  Register DATA (.D(ram_1_data), .en(DATA_write), .Q(DATA_q), .clk(CLOCK_out));  // open: clr
  alu alu_1 (
    .oper(in_1), .A(PC_q), .B(16'h1), .C_in(in_2), .Z(alu_1_z), .Result(alu_1_result), .C_out(alu_1_c_out),
    .N(alu_1_n), .V(alu_1_v));
  Register IR (.D(ram_1_data), .en(IR_write), .Q(IR_q), .clk(CLOCK_out));  // open: clr
endmodule

module alu (
  input  [3:0] oper,
  input  [15:0] A,
  input  [15:0] B,
  input  C_in,
  output Z,
  output [15:0] Result,
  output C_out,
  output N,
  output V
);

  wire adder_1_cout, subtractor_1_bout;
  wire [15:0] adder_1_out, subtractor_1_out;

  Adder #(.width(16)) adder_1 (.a(B), .b(A), .out(adder_1_out), .cin(C_in), .cout(adder_1_cout));
  Subtractor #(.width(16)) subtractor_1 (.a(A), .b(B), .out(subtractor_1_out), .bin(C_in), .bout(subtractor_1_bout));
  Multiplexer #(.select(4), .width(16)) multiplexer_1 (
    .in0(adder_1_out), .in1(subtractor_1_out), .out({N, Result[14:0]}), .sel(oper));  // open: in2, in3, in4, in5, in6, in7, in8, in9, in10, in11, in12, in13, in14, in15
  Multiplexer #(.select(4)) multiplexer_2 (
    .in0(adder_1_cout), .in1(subtractor_1_bout), .out(C_out), .sel(oper));  // open: in2, in3, in4, in5, in6, in7, in8, in9, in10, in11, in12, in13, in14, in15
  Pull_Resistor pull_resistor_1 (.node({N, Result[14:0]}));
  nor nor_1 (Z, Result[0], Result[1], Result[2], Result[3], Result[4], Result[5], Result[6], Result[7], Result[8], Result[9], Result[10], Result[11], Result[12], Result[13], Result[14], N);
  Pull_Resistor pull_resistor_2 (.node(C_out));
  overflow overflow_1 (.a(A[15]), .b(B[15]), .r(N), .v(V));
  Pull_Resistor pull_resistor_3 (.node(V));

  assign Result[15] = N;
endmodule

module overflow (
  input  a,
  input  b,
  input  r,
  output v
);

  wire and_1_out, and_2_out, and_3_out, and_4_out, not_1_out, not_2_out, not_3_out;

  not not_1 (not_1_out, a);
  not not_2 (not_2_out, b);
  and and_1 (and_1_out, not_1_out, not_2_out);
  and and_2 (and_2_out, a, b);
  not not_3 (not_3_out, r);
  and and_3 (and_3_out, and_1_out, r);
  and and_4 (and_4_out, and_2_out, not_3_out);
  or or_1 (v, and_3_out, and_4_out);
endmodule
